// Logisim project COUNTER.circ as structural Verilog: 1 circuit, main circuit main
module main (
  input  in_1,
  input  in_2,
  input  in_3,
  output out_4,
  output out_5,
  output out_6,
  output out_7,
  output out_8,
  output out_9,
  output out_10
);

  wire d_ff_1_qn, d_ff_2_qn, d_ff_3_qn, d_ff_4_qn, d_ff_5_qn, d_ff_6_qn, d_ff_7_qn, not_1_out, xor_1_out;

  not not_1 (not_1_out, in_1);
  D_Flip_Flop d_ff_1 (.clk(in_2), .D(d_ff_1_qn), .Q(out_8), .Qn(d_ff_1_qn));  // open: preset, en, reset
  D_Flip_Flop d_ff_2 (.clk(not_1_out), .D(d_ff_2_qn), .Q(out_5), .Qn(d_ff_2_qn));  // open: preset, en, reset
  D_Flip_Flop d_ff_3 (.clk(in_3), .D(d_ff_3_qn), .Q(out_10), .Qn(d_ff_3_qn));  // open: preset, en, reset
  D_Flip_Flop d_ff_4 (.clk(d_ff_1_qn), .D(d_ff_4_qn), .Q(out_7), .Qn(d_ff_4_qn));  // open: preset, en, reset
  D_Flip_Flop d_ff_5 (.clk(d_ff_2_qn), .D(d_ff_5_qn), .Q(out_4), .Qn(d_ff_5_qn));  // open: preset, en, reset
  D_Flip_Flop d_ff_6 (.clk(in_3), .D(xor_1_out), .Q(out_9), .Qn(d_ff_6_qn));  // open: preset, en, reset
  D_Flip_Flop d_ff_7 (.clk(out_7), .D(d_ff_7_qn), .Q(out_6), .Qn(d_ff_7_qn));  // open: preset, en, reset
  xor xor_1 (xor_1_out, d_ff_6_qn, d_ff_3_qn);

  // Notes on the sheet:
  //   2 BIT ASYNCHRONUS COUNTER
  //   3 BIT ASYNCHRONUS COUNTER
  //   2 BIT SYNCHRONUS COUNTER
endmodule
