// Logisim project Comparator.circ as structural Verilog
module main (
  input  in_1,
  input  in_2,
  output A_B,
  output A__B,
  output A_BOR_B_A
);

  wire not_1_out, not_2_out;

  not not_1 (not_1_out, in_1);
  not not_2 (not_2_out, in_2);
  and and_1 (A_B, in_1, not_2_out);
  xnor xnor_1 (A__B, in_1, in_2);
  and and_2 (A_BOR_B_A, not_1_out, in_2);
endmodule

module Comparator (
  input  in_1,
  input  in_2,
  input  in_3,
  input  in_4,
  output out_5,
  output out_6,
  output out_7
);

  wire main_1_a__b, main_1_a_b, main_1_a_bor_b_a, main_2_a__b, main_2_a_b, main_2_a_bor_b_a;

  main main_1 (.in_1(in_1), .in_2(in_2), .A_B(main_1_a_b), .A__B(main_1_a__b), .A_BOR_B_A(main_1_a_bor_b_a));
  main main_2 (.in_1(in_3), .in_2(in_4), .A_B(main_2_a_b), .A__B(main_2_a__b), .A_BOR_B_A(main_2_a_bor_b_a));
  and and_1 (out_5, main_1_a_b, main_2_a_b);
  and and_2 (out_6, main_1_a__b, main_2_a__b);
  and and_3 (out_7, main_1_a_bor_b_a, main_2_a_bor_b_a);
endmodule
