// Logisim project D-FLIPFLOP.circ as structural Verilog
module main (
  input  in_1,
  input  CLK,
  output out_3,
  output out_4
);

  wire and_1_out, and_2_out, not_1_out;

  not not_1 (not_1_out, in_1);
  and and_1 (and_1_out, in_1, CLK);
  and and_2 (and_2_out, CLK, not_1_out);
  nor nor_1 (out_3, and_1_out, out_4);
  nor nor_2 (out_4, and_2_out, out_3);
endmodule
