// Logisim project FULL ADDER.circ as structural Verilog
module main (
  input  A,
  input  B,
  input  CIN,
  output SUM,
  output COUT
);

  wire and_1_out, and_2_out, xor_1_out;

  and and_1 (and_1_out, A, B);
  xor xor_1 (xor_1_out, A, B);
  xor xor_2 (SUM, xor_1_out, CIN);
  and and_2 (and_2_out, xor_1_out, CIN);
  xor xor_3 (COUT, and_1_out, and_2_out);
endmodule
