// Logisim project HALF ADDER.circ as structural Verilog: 1 circuit, main circuit main
module main (
  input  in_1,
  input  in_2,
  output SUM,
  output CARRY
);

  xor xor_1 (SUM, in_1, in_2);
  and and_1 (CARRY, in_1, in_2);
endmodule
