// Logisim project LATCH CIRCUIT.circ as structural Verilog: 1 circuit, main circuit main
module main (
  input  in_1,
  input  CLK,
  output out_3,
  output out_4
);

  wire nand_1_out, nand_2_out;

  nand nand_1 (nand_1_out, in_1, CLK);
  nand nand_2 (nand_2_out, nand_1_out, CLK);
  nand nand_3 (out_3, nand_1_out, out_4);
  nand nand_4 (out_4, nand_2_out, out_3);
endmodule
