// Logisim project Multiplexer circuit.circ as structural Verilog
module main (
  input  I0,
  input  SEL,
  input  I1,
  output out_4
);

  wire and_1_out, and_2_out, not_1_out;

  not not_1 (not_1_out, SEL);
  and and_1 (and_1_out, I0, not_1_out);
  and and_2 (and_2_out, SEL, I1);
  or or_1 (out_4, and_1_out, and_2_out);
endmodule

module Multiplexer (
  input  in_1,
  input  in_2,
  input  [1:0] in_3,
  input  in_4,
  input  in_5,
  input  in_6,
  output out_7
);

  wire main_1_out_4, main_2_out_4;

  main main_1 (.I0(in_1), .SEL(in_3[0]), .I1(in_2), .out_4(main_1_out_4));
  main main_2 (.I0(in_4), .SEL(in_3[1]), .I1(in_6), .out_4(main_2_out_4));
  main main_3 (.I0(main_1_out_4), .SEL(in_5), .I1(main_2_out_4), .out_4(out_7));
endmodule
