// Logisim project XNOR GATE CIRCUIT.circ as structural Verilog: 1 circuit, main circuit main
module main (
  input  A,
  input  B,
  output out_3
);

  wire transistor_1_out, transistor_2_out, transistor_4_out, transistor_6_out, transistor_9_out,
       transistor_10_out, transistor_16_out;

  Transistor #(.\type ("n")) transistor_1 (.in(1'b1), .out(transistor_1_out), .gate(A));
  Transistor #(.\type ("n")) transistor_2 (.in(transistor_1_out), .out(transistor_2_out), .gate(B));
  Transistor transistor_3 (.in(1'b0), .out(transistor_2_out), .gate(A));
  Transistor transistor_4 (.in(1'b1), .out(transistor_4_out), .gate(A));
  Transistor #(.\type ("n")) transistor_5 (.in(1'b0), .out(transistor_4_out), .gate(A));
  Transistor transistor_6 (.in(1'b1), .out(transistor_6_out), .gate(B));
  Transistor #(.\type ("n")) transistor_7 (.in(1'b0), .out(transistor_6_out), .gate(B));
  Transistor transistor_8 (.in(1'b0), .out(transistor_2_out), .gate(B));
  Transistor #(.\type ("n")) transistor_9 (.in(1'b1), .out(transistor_9_out), .gate(transistor_4_out));
  Transistor #(.\type ("n")) transistor_10 (.in(transistor_9_out), .out(transistor_10_out), .gate(transistor_6_out));
  Transistor transistor_11 (.in(1'b0), .out(transistor_10_out), .gate(transistor_4_out));
  Transistor transistor_12 (.in(1'b0), .out(transistor_10_out), .gate(transistor_6_out));
  Transistor #(.\type ("n")) transistor_13 (.in(1'b1), .out(out_3), .gate(transistor_2_out));
  Transistor #(.\type ("n")) transistor_14 (.in(1'b1), .out(out_3), .gate(transistor_10_out));
  Transistor transistor_15 (.in(transistor_16_out), .out(out_3), .gate(transistor_2_out));
  Transistor transistor_16 (.in(1'b0), .out(transistor_16_out), .gate(transistor_10_out));
endmodule
