// Logisim project XOR GATE CIRCUIT.circ as structural Verilog: 1 circuit, main circuit main
module main (
  input  A,
  input  B,
  output out_3
);

  wire transistor_1_out, transistor_3_out, transistor_5_out, transistor_6_out, transistor_9_out,
       transistor_10_out, transistor_15_out;

  Transistor transistor_1 (.in(1'b1), .out(transistor_1_out), .gate(B));
  Transistor #(.\type ("n")) transistor_2 (.in(1'b0), .out(transistor_1_out), .gate(B));
  Transistor transistor_3 (.in(1'b1), .out(transistor_3_out), .gate(A));
  Transistor #(.\type ("n")) transistor_4 (.in(1'b0), .out(transistor_3_out), .gate(A));
  Transistor transistor_5 (.in(1'b0), .out(transistor_5_out), .gate(transistor_3_out));
  Transistor #(.\type ("n")) transistor_6 (.in(1'b1), .out(transistor_6_out), .gate(transistor_3_out));
  Transistor #(.\type ("n")) transistor_7 (.in(transistor_6_out), .out(transistor_5_out), .gate(B));
  Transistor transistor_8 (.in(1'b0), .out(transistor_5_out), .gate(B));
  Transistor transistor_9 (.in(1'b0), .out(transistor_9_out), .gate(A));
  Transistor #(.\type ("n")) transistor_10 (.in(1'b1), .out(transistor_10_out), .gate(A));
  Transistor #(.\type ("n")) transistor_11 (.in(transistor_10_out), .out(transistor_9_out), .gate(transistor_1_out));
  Transistor transistor_12 (.in(1'b0), .out(transistor_9_out), .gate(transistor_1_out));
  Transistor #(.\type ("n")) transistor_13 (.in(1'b1), .out(out_3), .gate(transistor_5_out));
  Transistor transistor_14 (.in(transistor_15_out), .out(out_3), .gate(transistor_5_out));
  Transistor transistor_15 (.in(1'b0), .out(transistor_15_out), .gate(transistor_9_out));
  Transistor #(.\type ("n")) transistor_16 (.in(1'b1), .out(out_3), .gate(transistor_9_out));
endmodule
